// Logisim project semáforo final.circ as structural Verilog: 4 circuits, main circuit semáforo
module \semáforo  (
  input  \Botão___Sensor_Velocidade 
);

  wire Carros_amarelo, Carros_out_5, Carros_vermelho, cronometro8_1_a, cronometro8_1_b, cronometro8_1_c,
       cronometro8_1_d, cronometro8_1_e, cronometro8_1_f, cronometro8_1_g, or_1_out, Pessoas_amarelo,
       Pessoas_verde, Pessoas_vermelho;

  or or_1 (or_1_out, Pessoas_amarelo, Pessoas_verde);
  \Semáfro_pessoas  Pessoas (
    .Vermelho(Pessoas_vermelho), .Amarelo(Pessoas_amarelo), .Verde(Pessoas_verde),
    .\Botão___Sensor_Velocidade (\Botão___Sensor_Velocidade ));
  \Semáfro_carros  Carros (
    .\Semáforo_Pessoas (or_1_out), .\Botão___Sensor_de_Velocidade (\Botão___Sensor_Velocidade ),
    .Vermelho(Carros_vermelho), .Amarelo(Carros_amarelo), .out_5(Carros_out_5));
  LED led_1 (.in(Pessoas_vermelho));
  LED led_2 (.in(Pessoas_amarelo));
  LED led_3 (.in(Pessoas_verde));
  LED led_4 (.in(Carros_vermelho));
  LED led_5 (.in(Carros_amarelo));
  LED led_6 (.in(Carros_out_5));
  Cronometro8 cronometro8_1 (
    .\Válido (Pessoas_verde), .A(cronometro8_1_a), .B(cronometro8_1_b), .C(cronometro8_1_c),
    .D(cronometro8_1_d), .E(cronometro8_1_e), .F(cronometro8_1_f), .G(cronometro8_1_g));
  _7_Segment_Display u_7_segment_display_1 (
    .g(cronometro8_1_g), .f(cronometro8_1_f), .a(cronometro8_1_a), .b(cronometro8_1_b), .e(cronometro8_1_e),
    .d(cronometro8_1_d), .c(cronometro8_1_c));  // open: dp
endmodule

module \Semáfro_carros  (
  input  \Semáforo_Pessoas ,
  input  \Botão___Sensor_de_Velocidade ,
  output Vermelho,
  output Amarelo,
  output out_5
);

  wire and_1_out, and_3_out, and_4_out, clock_1_out, not_1_out, or_1_out, or_2_out, X0_q, X0_qn, X1_q, X1_qn;

  not not_1 (not_1_out, \Semáforo_Pessoas );
  and and_1 (and_1_out, X0_q, not_1_out);
  or or_1 (or_1_out, X1_q, \Botão___Sensor_de_Velocidade );
  or or_2 (or_2_out, not_1_out, X1_qn);
  Clock clock_1 (.out(clock_1_out));
  J_K_Flip_Flop X1 (.J(X0_q), .clk(clock_1_out), .K(and_1_out), .Q(X1_q), .Qn(X1_qn));  // open: preset, en, reset
  J_K_Flip_Flop X0 (.J(or_1_out), .clk(clock_1_out), .K(or_2_out), .Q(X0_q), .Qn(X0_qn));  // open: preset, en, reset
  and and_2 (Vermelho, X1_q, X0_q);
  and and_3 (and_3_out, X1_qn, X0_q);
  or or_3 (Amarelo, and_3_out, and_4_out);
  and and_4 (and_4_out, X1_q, X0_qn);
  and and_5 (out_5, X1_qn, X0_qn);
endmodule

module \Semáfro_pessoas  (
  input  \Botão___Sensor_Velocidade ,
  output Vermelho,
  output Amarelo,
  output Verde
);

  wire and_1_out, and_2_out, and_3_out, and_4_out, and_5_out, and_6_out, and_7_out, and_8_out, and_9_out,
       and_10_out, and_11_out, and_12_out, and_13_out, and_14_out, and_15_out, and_16_out, and_17_out,
       and_18_out, and_19_out, and_20_out, and_21_out, and_22_out, and_23_out, and_24_out, and_25_out,
       and_26_out, and_27_out, and_28_out, and_29_out, and_30_out, and_31_out, clock_1_out, not_1_out,
       not_2_out, or_1_out, or_2_out, or_3_out, or_4_out, or_5_out, or_6_out, or_7_out, X0_q, X0_qn, X1_q,
       X1_qn, X2_q, X2_qn, X3_q, X3_qn;

  not not_1 (not_1_out, \Botão___Sensor_Velocidade );
  and and_1 (and_1_out, X1_q, X0_q, not_1_out);
  and and_2 (and_2_out, X1_q, X0_q, \Botão___Sensor_Velocidade );
  and and_3 (and_3_out, X1_q, X0_q, not_1_out);
  and and_4 (and_4_out, X1_q, X0_q, \Botão___Sensor_Velocidade );
  and and_5 (and_5_out, X0_q, not_1_out);
  and and_6 (and_6_out, X0_q, \Botão___Sensor_Velocidade );
  and and_7 (and_7_out, X0_q, not_1_out);
  and and_8 (and_8_out, X0_q, \Botão___Sensor_Velocidade );
  and and_9 (and_9_out, X1_q, not_1_out);
  and and_10 (and_10_out, X2_q, not_1_out);
  and and_11 (and_11_out, X3_q, not_1_out);
  and and_12 (and_12_out, X2_q, X1_q, X0_q, not_1_out);
  and and_13 (and_13_out, X2_q, X1_q, X0_q, \Botão___Sensor_Velocidade );
  and and_14 (and_14_out, X2_q, X1_q, X0_q, not_1_out);
  and and_15 (and_15_out, X2_q, X1_q, X0_q, \Botão___Sensor_Velocidade );
  Clock clock_1 (.out(clock_1_out));
  or or_1 (or_1_out, and_12_out, and_13_out);
  or or_2 (or_2_out, and_14_out, and_15_out);
  or or_3 (or_3_out, and_1_out, and_2_out);
  or or_4 (or_4_out, and_3_out, and_4_out);
  or or_5 (or_5_out, and_5_out, and_6_out);
  or or_6 (or_6_out, and_7_out, and_8_out);
  or or_7 (or_7_out, and_9_out, and_10_out, \Botão___Sensor_Velocidade , and_11_out);
  J_K_Flip_Flop X3 (.J(or_1_out), .clk(clock_1_out), .K(or_2_out), .Q(X3_q), .Qn(X3_qn));  // open: preset, en, reset
  J_K_Flip_Flop X2 (.J(or_3_out), .clk(clock_1_out), .K(or_4_out), .Q(X2_q), .Qn(X2_qn));  // open: preset, en, reset
  J_K_Flip_Flop X1 (.J(or_5_out), .clk(clock_1_out), .K(or_6_out), .Q(X1_q), .Qn(X1_qn));  // open: preset, en, reset
  J_K_Flip_Flop X0 (.J(or_7_out), .clk(clock_1_out), .K(1'b1), .Q(X0_q), .Qn(X0_qn));  // open: preset, en, reset
  not not_2 (not_2_out, \Botão___Sensor_Velocidade );
  and and_16 (and_16_out, X1_qn, X2_qn, X3_qn, not_2_out);
  and and_17 (and_17_out, X1_qn, X2_qn, X3_qn, \Botão___Sensor_Velocidade );
  and and_18 (and_18_out, X0_qn, X3_qn, X2_qn, not_2_out);
  and and_19 (and_19_out, X0_qn, X3_qn, X2_qn, \Botão___Sensor_Velocidade );
  and and_20 (and_20_out, X3_q, X2_q, X1_q, X0_q, \Botão___Sensor_Velocidade );
  and and_21 (and_21_out, X3_q, X2_q, X1_q, X0_q, not_2_out);
  and and_22 (and_22_out, X3_q, X2_q, X1_qn, not_2_out);
  and and_23 (and_23_out, X3_q, X2_q, X1_qn, \Botão___Sensor_Velocidade );
  and and_24 (and_24_out, X3_qn, X0_q, X1_q, not_2_out);
  and and_25 (and_25_out, X3_qn, X2_q, not_2_out);
  and and_26 (and_26_out, X3_qn, X2_q, \Botão___Sensor_Velocidade );
  and and_27 (and_27_out, X3_q, X2_qn, \Botão___Sensor_Velocidade );
  and and_28 (and_28_out, X3_q, X2_qn, not_2_out);
  and and_29 (and_29_out, X3_qn, X1_q, X0_q, \Botão___Sensor_Velocidade );
  and and_30 (and_30_out, X3_q, X2_q, X0_qn, \Botão___Sensor_Velocidade );
  and and_31 (and_31_out, X3_q, X2_q, X0_qn, not_2_out);
  or or_8 (Vermelho, and_16_out, and_17_out, and_18_out, and_19_out, and_20_out, and_21_out);
  or or_9 (Verde, and_24_out, and_25_out, and_26_out, and_27_out, and_28_out, and_29_out);
  or or_10 (Amarelo, and_22_out, and_23_out, and_30_out, and_31_out);
endmodule

module Cronometro8 (
  input  \Válido ,
  output A,
  output B,
  output C,
  output D,
  output E,
  output F,
  output G
);

  wire and_1_out, and_2_out, and_3_out, and_4_out, and_5_out, and_6_out, and_7_out, and_8_out, and_9_out,
       and_10_out, and_11_out, and_12_out, and_13_out, and_14_out, and_15_out, and_16_out, and_17_out,
       and_18_out, and_19_out, and_20_out, and_21_out, and_22_out, and_23_out, and_24_out, and_25_out,
       and_26_out, and_27_out, and_28_out, and_29_out, and_30_out, and_31_out, and_32_out, and_33_out,
       and_34_out, and_35_out, and_36_out, and_37_out, and_38_out, and_39_out, and_40_out, and_41_out,
       and_42_out, and_43_out, and_44_out, and_45_out, and_46_out, and_47_out, and_48_out, and_49_out,
       and_50_out, and_51_out, clock_1_out, not_1_out, not_2_out, or_1_out, or_2_out, or_3_out, or_4_out,
       or_5_out, or_6_out, X0_q, X0_qn, X1_q, X1_qn, X2_q, X2_qn, X3_qn;

  not not_1 (not_1_out, \Válido );
  and and_1 (and_1_out, X0_q, X1_q, X2_q, \Válido );
  and and_2 (and_2_out, X0_q, X1_q, X2_q, not_1_out);
  and and_3 (and_3_out, X1_q, X0_q, \Válido );
  and and_4 (and_4_out, X1_q, X0_q, not_1_out);
  and and_5 (and_5_out, X0_q, X1_q, not_1_out);
  and and_6 (and_6_out, X0_q, X1_q, \Válido );
  and and_7 (and_7_out, X0_q, not_1_out);
  and and_8 (and_8_out, X0_q, \Válido );
  and and_9 (and_9_out, X0_q, not_1_out);
  and and_10 (and_10_out, X0_q, \Válido );
  and and_11 (and_11_out, X3_qn, \Válido );
  and and_12 (and_12_out, X1_q, not_1_out);
  and and_13 (and_13_out, X2_q, not_1_out);
  or or_1 (or_1_out, and_1_out, and_2_out);
  or or_2 (or_2_out, and_3_out, and_4_out);
  or or_3 (or_3_out, and_5_out, and_6_out);
  or or_4 (or_4_out, and_7_out, and_8_out);
  or or_5 (or_5_out, and_9_out, and_10_out);
  or or_6 (or_6_out, and_11_out, and_12_out, and_13_out);
  Clock clock_1 (.out(clock_1_out));
  J_K_Flip_Flop X3 (.J(or_1_out), .clk(clock_1_out), .K(1'b1), .Qn(X3_qn));  // open: Q, preset, en, reset
  J_K_Flip_Flop X2 (.J(or_2_out), .clk(clock_1_out), .K(or_3_out), .Q(X2_q), .Qn(X2_qn));  // open: preset, en, reset
  J_K_Flip_Flop X1 (.J(or_4_out), .clk(clock_1_out), .K(or_5_out), .Q(X1_q), .Qn(X1_qn));  // open: preset, en, reset
  J_K_Flip_Flop X0 (.J(or_6_out), .clk(clock_1_out), .K(1'b1), .Q(X0_q), .Qn(X0_qn));  // open: preset, en, reset
  not not_2 (not_2_out, \Válido );
  and and_14 (and_14_out, not_2_out, X2_qn);
  and and_15 (and_15_out, \Válido , X2_qn);
  and and_16 (and_16_out, X1_qn, X0_q, \Válido );
  and and_17 (and_17_out, X1_qn, X0_q, not_2_out);
  and and_18 (and_18_out, X0_qn, X1_q, not_2_out);
  and and_19 (and_19_out, X0_qn, X1_q, \Válido );
  and and_20 (and_20_out, X1_qn, \Válido );
  and and_21 (and_21_out, X1_qn, not_2_out);
  and and_22 (and_22_out, X2_q, not_2_out);
  and and_23 (and_23_out, X2_q, \Válido );
  and and_24 (and_24_out, X2_qn, \Válido );
  and and_25 (and_25_out, \Válido , X1_qn);
  and and_26 (and_26_out, X0_q, \Válido );
  and and_27 (and_27_out, X2_qn, not_2_out);
  and and_28 (and_28_out, X1_qn, not_2_out);
  and and_29 (and_29_out, X0_q, not_2_out);
  and and_30 (and_30_out, X2_qn, X0_qn, not_2_out);
  and and_31 (and_31_out, X2_qn, X0_qn, \Válido );
  and and_32 (and_32_out, X0_qn, X1_q, not_2_out);
  and and_33 (and_33_out, X0_qn, X1_q, \Válido );
  and and_34 (and_34_out, X2_qn, X1_q, \Válido );
  and and_35 (and_35_out, X2_qn, X1_q, not_2_out);
  and and_36 (and_36_out, X2_q, X1_qn, X0_q, \Válido );
  and and_37 (and_37_out, X2_q, X1_qn, X0_q, not_2_out);
  and and_38 (and_38_out, X2_qn, X0_qn, \Válido );
  and and_39 (and_39_out, X2_qn, X0_qn, not_2_out);
  and and_40 (and_40_out, X1_q, X0_qn, \Válido );
  and and_41 (and_41_out, X1_q, X0_qn, not_2_out);
  and and_42 (and_42_out, X1_qn, X0_qn, \Válido );
  and and_43 (and_43_out, X1_qn, X0_qn, not_2_out);
  and and_44 (and_44_out, X2_qn, X1_q, \Válido );
  and and_45 (and_45_out, X2_qn, X1_q, not_2_out);
  and and_46 (and_46_out, X3_qn, X0_qn, not_2_out);
  and and_47 (and_47_out, X3_qn, X0_qn, \Válido );
  and and_48 (and_48_out, X2_q, X1_qn, not_2_out);
  and and_49 (and_49_out, X2_q, X1_qn, \Válido );
  and and_50 (and_50_out, X2_qn, X1_q, not_2_out);
  and and_51 (and_51_out, X2_qn, X1_q, \Válido );
  or or_7 (A, and_14_out, and_15_out, and_16_out, and_17_out, and_18_out, and_19_out);
  or or_8 (B, and_20_out, and_21_out, and_22_out, and_23_out);
  or or_9 (C, and_24_out, and_25_out, and_26_out, and_27_out, and_28_out, and_29_out);
  or or_10 (D, and_30_out, and_31_out, and_32_out, and_33_out, and_34_out, and_35_out, and_36_out, and_37_out);
  or or_11 (E, and_38_out, and_39_out, and_40_out, and_41_out);
  or or_12 (F, and_42_out, and_43_out, and_44_out, and_45_out);
  or or_13 (G, and_46_out, and_47_out, and_48_out, and_49_out, and_50_out, and_51_out);
endmodule
